# Fritzing sketch ElectricBlanket (saved by Fritzing 0.9.2b)
breadboards: 1

parts:
  U1 = atmega328 [package=dip]
  S1 = Pushbutton [package="[THT]"]
  XTAL1 = CRYSTAL - kHz [frequency="16 Mhz"]
  C1 = Ceramic Capacitor [capacitance=22pF package="100 mil [THT, multilayer]"]
  C2 = Ceramic Capacitor [capacitance=100nF package="100 mil [THT, multilayer]"]
  R1 = Resistor [tolerance=±5% resistance=10k package=THT]
  D1 = Diode [package=diode-1n4148]
  부품1 = Bluetooth Mate Silver
  RHT1 = Humidity and Temperature Sensor RHT03
  R2 = Resistor [tolerance=±5% resistance=10k package=THT]
  U2 = RELAY [package=relay-g5q]
  U3 = RELAY [package=relay-g5q]
  Q1 = NPN-Transistor [package="TO92 [THT]"]
  Q2 = NPN-Transistor [package="TO92 [THT]"]
  D2 = Rectifier Diode [part_number=1N4001 package="300 mil [THT]"]
  D3 = Rectifier Diode [part_number=1N4001 package="300 mil [THT]"]

nets:
  N1: U1.RESET, S1.Pin_1, S1.Pin_2, R1.Pin_0, D1.A
  N2: U1.D2, RHT1.Data-signal, R2.Pin_0
  VCC: U1.VCC, R1.Pin_1, D1.C, 부품1.VCC, RHT1.Vcc, R2.Pin_1
  N3: U1.GND#7, S1.Pin_3, S1.Pin_4, C1.1, C2.1, 부품1.GND, RHT1.GND_2, Q1.E, Q2.E
  N4: U1.XLAT1, XTAL1.pin_0, C1.0
  N5: U1.XLAT2, XTAL1.pin_1, C2.0
  N6: U1.D8, 부품1.TX_5V
  N7: U1.D9_(PWM), 부품1.RX_5V
  N8: U1.D10_(PWM), Q1.B
  N9: U1.D11_(PWM), Q2.B
  N10: U1.AVCC, U1.AREF, U2.COIL2, U3.COIL2, D2.cathode, D3.cathode
  N11: U2.COIL1, Q1.C, D2.anode
  N12: U3.COIL1, Q2.C, D3.anode
