# Fritzing sketch HomeServer (saved by Fritzing 0.9.2b)
breadboards: 1

parts:
  Raspberry_Pi1 = Raspberry Pi 2
  DHT1 = DHT11 Humitidy and Temperature Sensor
  R1 = Resistor [tolerance=±5% resistance=4.7k package=THT]
  U1 = RF-LINK_TX [package=rf-link_tx]
  U2 = RELAY [package=relay-jzc]
  Q1 = NPN-Transistor [package="TO92 [THT]"]
  R2 = Resistor [tolerance=±5% resistance=1k package=THT]
  J1 = female pin header, 2 pins [form="♀ (female)"]
  J1_2 = male pin header, 2 pins [form="♂ (male)"]
  S1 = Pushbutton [package="[THT]"]
  R3 = Resistor [tolerance=±5% resistance=1k package=THT]
  R4 = Resistor [tolerance=±0.1% resistance=10k package=THT]
  D1 = Rectifier Diode [part_number=1N4001 package="300 mil [THT]"]

nets:
  3V3: Raspberry_Pi1.3v3, DHT1.VDD, R1.Pin_1, U1.+5V, S1.Pin_1, S1.Pin_2
  N1: Raspberry_Pi1.GPIO17, DHT1.DATA, R1.Pin_0
  N2: Raspberry_Pi1.GPIO22, R2.Pin_0
  N3: Raspberry_Pi1.GPIO23, R3.Pin_1
  N4: Raspberry_Pi1.GPIO18, U1.DATA
  GND: Raspberry_Pi1.GND, DHT1.GND, U1.GND, Q1.E, R4.Pin_1
  N5: Raspberry_Pi1.5V, U2.COIL1, D1.cathode
  N6: U2.COIL2, Q1.C, D1.anode
  N7: U2.NO, J1.pin2, J1_2.pin2
  N8: U2.MAIN, J1.pin1, J1_2.pin1
  N9: Q1.B, R2.Pin_1
  N10: S1.Pin_3, S1.Pin_4, R3.Pin_0, R4.Pin_0

custom parts:
  DHT11 Humitidy and Temperature Sensor: DHT11 Humidity and Temperature Sensor
