# Fritzing sketch WallSwitch (saved by Fritzing 0.9.3b)
breadboards: 1

parts:
  IC1 = MICROCONTROLLER [package=dil28-3-zif_socket]
  S1 = Pushbutton [package="[THT]"]
  R1 = Resistor [tolerance=±5% resistance=10k package=THT]  # not connected
  D1 = Diode [package=diode-1n4148]
  XTAL1 = CRYSTAL - kHz [frequency="16 Mhz"]
  C1 = Ceramic Capacitor [capacitance=0.22nF package="100 mil [THT, multilayer]"]
  C2 = Ceramic Capacitor [capacitance=0.22nF package="100 mil [THT, multilayer]"]
  C3 = Ceramic Capacitor [capacitance=100nF package="100 mil [THT, multilayer]"]
  U1 = RF-LINK_RX [package=rf-link_rx]
  R2 = Resistor [tolerance=±5% resistance=10k package=THT]
  S2 = Toggle Switch [package=THT]

nets:
  N1: IC1.PC6(_RESET), S1.Pin_1, S1.Pin_2, D1.A
  N2: IC1.PD4(XCK_T0), R2.Pin_0, S2.L1
  VCC: IC1.VCC, IC1.AVCC, IC1.AREF, D1.C, C3.0, U1.+5V
  GND: IC1.GND, IC1.AGND, S1.Pin_3, S1.Pin_4, C1.1, C2.1, C3.1, U1.GND, R2.Pin_1, S2.COM
  N3: IC1.PB6(XTAL1_TOSC1), XTAL1.pin_0, C1.0
  N4: IC1.PB7(XTAL2_TOSC2), XTAL1.pin_1, C2.0

notes:
  Relay Module
  Input(Low active)
